# Fritzing sketch esp32_ft232hl (saved by Fritzing 0.9.3b)

parts:
  Part1 = Adafruit FT232H Breakout [part_number="Adafruit #2264"]
  U2 = ESP32-38PinWide [part_number=ESP32-38PinWide]

nets:
  GND: Part1.GND, U2.GND
  N1: Part1.D0, U2.GPIO13
  N2: Part1.D1, U2.GPIO12
  N3: Part1.D2, U2.GPIO15
  N4: Part1.D3, U2.GPIO14

custom parts:
  Adafruit FT232H Breakout: Wouldn't it be cool to drive a tiny OLED display, read a color sensor, or even just flash some LEDs directly from your computer? Sure you can program an Arduino or Trinket to talk to these devices and your computer, but why can't your computer just talk to those devices and sensors itself? Well, now your computer can talk to devices using the Adafruit FT232H breakout board! What can the FT232H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
  ESP32-38PinWide: Generic 38-Pin ESP32 with wide format (only access to one side of pins on a breadboard) based on Stephen Lilley's HiLetgo ESP-WROOM-32 ESP32 ESP-32S Development Board.
