# Fritzing sketch wiring (saved by Fritzing 0.9.3b)
breadboards: 1

parts:
  M1 = STM32F103C8T6 blue mini board
  J1 = shrouded pin header, 10 pins [form="♂ (shrouded male)"]

nets:
  N1: M1.G, M1.B11, M1.GND, J1.pin9
  N2: M1.3.3V, M1.B1, M1.3.3, J1.pin7
  N3: M1.B10, M1.connector45, M1.Boot0
  N4: M1.DIO, J1.pin10
  N5: M1.CLK, J1.pin8

notes:
  ST-LINK V2

custom parts:
  STM32F103C8T6 blue mini board: Generic Blue Pill microcomputer module, available from Ebay and others. CPU STM32F103C8 72Mhz Flash: 64 KB/128 KB RAM: 20KB.
